# Fritzing sketch supercold_fritzing (saved by Fritzing 1.0.4)
breadboards: 1

parts:
  Mod1 = ESP32-TTGO-T-DISPLAY
  Part1 = Black Joystick KY-023
  Part2 = Black Joystick KY-023
  S1 = Pushbutton [package="[THT]"]

nets:
  GND: Mod1.G-1, Mod1.G-2, Mod1.G-10, Mod1.G-11, Mod1.G-14, Part1.GND, Part2.GND, S1.Pin_1, S1.Pin_2
  N1: Mod1.21, S1.Pin_3, S1.Pin_4
  N2: Mod1.15, Part2.SW
  N3: Mod1.13, Part2.VRy
  N4: Mod1.12, Part2.VRx
  +5V: Mod1.3V, Part1.+5V, Part2.+5V
  N5: Mod1.32, Part1.SW
  N6: Mod1.39, Part1.VRy
  N7: Mod1.38, Part1.VRx

custom parts:
  ESP32-TTGO-T-DISPLAY: LILYGO TTGO T-Display GD32VF103CBT6 Main Chip ST7789 1.14 Inch IPS 240x135 Resolution Minimalist Development Board.
  Black Joystick KY-023: Description: The joystick is a combination of 2 analoog potentiometer and a digital switch. Arduino GND --> Module pin - Arduino +5V --> Module pin +5V Arduino Analoog 0 --> Module VRx Arduino Analoog 1 --> Module VRy Arduino Digital --> Module SW Dimensions: 1" x 1.25"
